# Fritzing sketch RPiGameDevice (saved by Fritzing 0.9.3b)
breadboards: 5

parts:
  IC1 = MCP3008 8-channel 10-bit ADC [part_number=MCP3008]
  Raspberry_Pi1 = Raspberry Pi 2
  Part1 = Thumb Joystick
  Part2 = Thumb Joystick
  S1 = Momentary Switch [package=ksa_sealed_tac_switch]
  S2 = Momentary Switch [package=ksa_sealed_tac_switch]
  S3 = Momentary Switch [package=ksa_sealed_tac_switch]
  S4 = Momentary Switch [package=ksa_sealed_tac_switch]
  S5 = Momentary Switch [package=ksa_sealed_tac_switch]
  S6 = Momentary Switch [package=ksa_sealed_tac_switch]
  S7 = Momentary Switch [package=ksa_sealed_tac_switch]
  S8 = Momentary Switch [package=ksa_sealed_tac_switch]
  S9 = Momentary Switch [package=ksa_sealed_tac_switch]
  S10 = Momentary Switch [package=ksa_sealed_tac_switch]
  R1 = Resistor [tolerance=±5% resistance=1k package="1206 [SMD]"]
  R3 = Resistor [tolerance=±5% resistance=10k package="1206 [SMD]"]
  R4 = Resistor [tolerance=±5% resistance=1k package="1206 [SMD]"]
  R5 = Resistor [tolerance=±5% resistance=10k package="1206 [SMD]"]
  R6 = Resistor [tolerance=±5% resistance=1k package="1206 [SMD]"]
  R7 = Resistor [tolerance=±5% resistance=10k package="1206 [SMD]"]
  R8 = Resistor [tolerance=±5% resistance=1k package="1206 [SMD]"]
  R9 = Resistor [tolerance=±5% resistance=10k package="1206 [SMD]"]
  R10 = Resistor [tolerance=±5% resistance=1k package="1206 [SMD]"]
  R11 = Resistor [tolerance=±5% resistance=10k package="1206 [SMD]"]
  R12 = Resistor [tolerance=±5% resistance=1k package="1206 [SMD]"]
  R13 = Resistor [tolerance=±5% resistance=10k package="1206 [SMD]"]
  R14 = Resistor [tolerance=±5% resistance=1k package="1206 [SMD]"]
  R15 = Resistor [tolerance=±5% resistance=10k package="1206 [SMD]"]
  R16 = Resistor [tolerance=±5% resistance=1k package="1206 [SMD]"]
  R17 = Resistor [tolerance=±5% resistance=10k package="1206 [SMD]"]
  R18 = Resistor [tolerance=±5% resistance=1k package="1206 [SMD]"]
  R19 = Resistor [tolerance=±5% resistance=10k package="1206 [SMD]"]
  R20 = Resistor [tolerance=±5% resistance=1k package="1206 [SMD]"]
  R21 = Resistor [tolerance=±5% resistance=10k package="1206 [SMD]"]
  Part4 = Adafruit PowerBoost 1000C [part_number="Adafruit #2465"]
  Part5 = Adafruit Trinket 3V [part_number="Adafruit #1500"]
  U1 = LIPO-2000mAh [package=lipo-2000]  # not connected
  R22 = Resistor [tolerance=±5% resistance=6.8k package=THT]
  R23 = Resistor [tolerance=±5% resistance=6.8k package=THT]
  R24 = Resistor [tolerance=±5% resistance=10k package=THT]
  R25 = Resistor [tolerance=±5% resistance=10k package=THT]
  S12 = Momentary Switch [package=ksa_sealed_tac_switch]
  R26 = Resistor [tolerance=±5% resistance=10k package="1206 [SMD]"]
  R27 = Resistor [tolerance=±5% resistance=1k package="1206 [SMD]"]
  S13 = Momentary Switch [package=ksa_sealed_tac_switch]
  R28 = Resistor [tolerance=±5% resistance=10k package="1206 [SMD]"]
  R29 = Resistor [tolerance=±5% resistance=1k package="1206 [SMD]"]
  S14 = Pushbutton [package="[THT]"]
  R31 = Resistor [tolerance=±5% resistance=16k package=THT]
  R32 = Resistor [tolerance=±5% resistance=10k package=THT]
  R33 = Resistor [tolerance=±5% resistance=100 package=THT]
  R34 = Resistor [tolerance=±5% resistance=100 package=THT]
  R35 = Resistor [tolerance=±5% resistance=100 package=THT]
  R36 = Resistor [tolerance=±5% resistance=100 package=THT]
  LED1 = LED - 3mm [color="Red (633nm)" package="3 mm [THT]"]
  LED2 = LED - 3mm [color="Red (633nm)" package="3 mm [THT]"]
  LED3 = LED - 3mm [color="Red (633nm)" package="3 mm [THT]"]
  LED4 = LED - 3mm [color="Red (633nm)" package="3 mm [THT]"]

nets:
  N1: IC1.no_name_yet#1, R23.Pin_0, R25.Pin_1
  N2: IC1.no_name_yet#2, R22.Pin_0, R24.Pin_0
  N3: IC1.no_name_yet#3, Part1.SEL
  N4: IC1.no_name_yet#4, Part1.HORZ
  N5: IC1.no_name_yet#5, Part1.VERT
  N6: IC1.no_name_yet#6, Part2.SEL
  N7: IC1.no_name_yet#7, Part2.HORZ
  N8: IC1.no_name_yet#8, Part2.VERT
  GND: IC1.no_name_yet#9, IC1.no_name_yet#14, Raspberry_Pi1.GND, Part1.GND, Part2.GND, R3.Pin_0, R5.Pin_0, R7.Pin_0, R9.Pin_0, R11.Pin_0, R15.Pin_0, R17.Pin_0, R19.Pin_0, R21.Pin_0, Part4.GND, Part5.GND, R24.Pin_1, R25.Pin_0, R28.Pin_0, R32.Pin_1, R33.Pin_0, R35.Pin_0, R36.Pin_0
  N9: IC1.no_name_yet#10, Raspberry_Pi1.GPIO8
  N10: IC1.no_name_yet#11, Raspberry_Pi1.GPIO10
  N11: IC1.no_name_yet#12, Raspberry_Pi1.GPIO9
  N12: IC1.no_name_yet#13, Raspberry_Pi1.GPIO11
  3V3: IC1.no_name_yet#15, IC1.no_name_yet#16, Raspberry_Pi1.3v3, Raspberry_Pi1.3V3, Part1.VCC, Part2.VCC, S1.2, S3.2, S4.2, S5.2, S6.2, S7.2, S9.2, S10.2, Part5.VBAT, S12.2, S13.2
  N13: Raspberry_Pi1.GPIO4, LED1.anode
  N14: Raspberry_Pi1.GPIO17, R27.Pin_0
  N15: Raspberry_Pi1.GPIO27, R20.Pin_0
  N16: Raspberry_Pi1.GPIO22, R10.Pin_0
  N17: Raspberry_Pi1.GPIO5, LED2.anode
  N18: Raspberry_Pi1.GPIO6, LED3.anode
  N19: Raspberry_Pi1.GPIO19, R4.Pin_0
  N20: Raspberry_Pi1.GPIO26, R18.Pin_0
  N21: Raspberry_Pi1.GPIO21, R8.Pin_0
  N22: Raspberry_Pi1.GPIO20, R6.Pin_0
  N23: Raspberry_Pi1.GPIO16, R29.Pin_0
  N24: Raspberry_Pi1.GPIO7, LED4.anode
  N25: Raspberry_Pi1.GPIO25, R16.Pin_0
  N26: Raspberry_Pi1.GPIO24, R14.Pin_0
  N27: Raspberry_Pi1.GPIO23, R12.Pin_0
  N28: Raspberry_Pi1.GPIO18, R1.Pin_0
  N29: Raspberry_Pi1.GPIO15, Part5.#1
  N30: Raspberry_Pi1.GPIO14, R31.Pin_0
  N31: Raspberry_Pi1.5V, Part4.5.0V
  N32: S1.3, R1.Pin_1
  N33: S1.4, R3.Pin_1
  N34: S2.3, R4.Pin_1
  N35: S2.4, R5.Pin_1
  N36: S3.3, R6.Pin_1
  N37: S3.4, R7.Pin_1
  N38: S4.3, R8.Pin_1
  N39: S4.4, R9.Pin_1
  N40: S5.3, R10.Pin_1
  N41: S5.4, R11.Pin_1
  N42: S6.3, R12.Pin_1
  N43: S6.4, R13.Pin_1
  N44: S7.3, R20.Pin_1
  N45: S7.4, R21.Pin_1
  N46: S8.3, R16.Pin_1
  N47: S8.4, R17.Pin_1
  N48: S9.3, R18.Pin_1
  N49: S9.4, R19.Pin_1
  N50: S10.3, R14.Pin_1
  N51: S10.4, R15.Pin_1
  N52: Part4.VBUS, R22.Pin_1
  N53: Part4.VLIPO, R23.Pin_1, S14.Pin_3, S14.Pin_4
  N54: Part4.ENABLE, Part5.#2, S14.Pin_1, S14.Pin_2, R31.Pin_1, R32.Pin_0
  N55: Part4.LBO, Part5.#0
  N56: S12.3, R27.Pin_1
  N57: S12.4, R26.Pin_1
  N58: S13.3, R29.Pin_1
  N59: S13.4, R28.Pin_1
  N60: R33.Pin_1, LED1.cathode
  N61: R34.Pin_1, LED2.cathode
  N62: R35.Pin_1, LED3.cathode
  N63: R36.Pin_1, LED4.cathode

notes:
  GPIO Pinout
  8: MCP3008 CS
  9: MCP3008 DOUT
  10: MCP3008 DIN
  11: MCP3008 CLK
  14: Reads power button press
  15: Writes to trinket to notify of power off (LOW will notify of poweroff)
  16-27: game buttons
  Trinket Pinout
  #0: Reads LBO from PowerBoost
  #1: When LOW will wait > 1:15 before powering off
  #2: Sets PowerBoost EN pin high/low
  MCP3008 Pinout
  Channel #
  0: Joystick 1 VERT
  1: Joystick 1 HORZ
  2: Joystick 1 Button
  3: Joystick 1 VERT
  4: Joystick 1 HORZ
  5: Joystick 1 Button
  6: PowerBoost BAT
  7: PowerBoost USB

custom parts:
  Adafruit PowerBoost 1000C: PowerBoost 1000C is the perfect power supply for your portable project! With a built-in load-sharing battery charger circuit, you'll be able to keep your power-hungry project running even while recharging the battery! This little DC/DC boost converter module can be powered by any 3.7V LiIon/LiPoly battery, and convert the battery output to 5.2V DC for running your 5V projects.
  Adafruit Trinket 3V: Trinket may be small, but do not be fooled by its size! It's a tiny microcontroller board, built around the Atmel ATtiny85, a little chip with a lot of power. We wanted to design a microcontroller board that was small enough to fit into any project, and low cost enough to use without hesitation. Perfect for when you don't want to give up your expensive dev-board and you aren't willing to take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
